# Fritzing sketch SqueezeBulb_Lamp_circuit (saved by Fritzing 0.9.3b)
breadboards: 1

parts:
  Part2 = Arduino MKR1000
  U1 = LM 358 Dual Op-Amp [package="DIP8 [THT]"]
  MPX1 = MPX2010 pressure sensor [part_number=MPX]  # not connected
  R2 = Resistor [tolerance=±5% resistance=100k package=THT]
  R4 = Resistor [tolerance=±5% resistance=470k package=THT]
  R3 = Resistor [tolerance=±5% resistance=1k package=THT]
  R1 = Resistor [tolerance=±5% resistance=1k package=THT]
  R5 = Resistor [tolerance=±5% resistance=1k package=THT]
  U2 = POT [package=alps_pot]  # not connected
  Q1 = TIP120 Hi-Current Darlington Transistor
  JACK1 = 2.1mm Barrel Jack with Terminal Block
  R6 = Resistor [tolerance=±5% resistance=1k package=THT]
  Q2 = TIP120 Hi-Current Darlington Transistor
  LED1 = LEDs [package=led-1206]  # not connected
  LED2 = LEDs [package=led-1206]  # not connected

nets:
  3.3V: Part2.VCC
  GND: Part2.GND, U1.connector3, R4.Pin_0, Q1.EMITTER, JACK1.NEG, Q2.EMITTER
  N1: Part2.D4_PWM, R5.Pin_0
  N2: Part2.A0/DAC0, U1.connector0, R2.Pin_1
  N3: U1.connector1, R2.Pin_0, R1.Pin_0
  N4: U1.connector2, R4.Pin_1, R3.Pin_0
  N5: R5.Pin_1, Q1.BASE
  N6: R6.Pin_1, Q2.BASE

custom parts:
  Arduino MKR1000: MKR1000 is a powerful board that combines the functionality of the Zero and the Wi-Fi Shield. It is the ideal solution for makers wanting to design IoT projects with minimal previous experience in networking
