# Fritzing sketch 555LEDFader (saved by Fritzing 0.9.4)
breadboards: 1

parts:
  U2 = 555 Timer [package="DIP8 [THT]"]
  R1 = Resistor [tolerance=±5% resistance=10k package="0603 [SMD]"]
  R2 = Resistor [tolerance=±5% resistance=1k package="0603 [SMD]"]
  Q1 = Basic FET N-Channel [package="TO220 [THT]"]
  U3 = POT [package=alps_pot]
  C1 = Tantalum Capacitor [capacitance="1 μF" package="A 3216 [SMD, tantalum]"]
  C2 = Tantalum Capacitor [capacitance="1 μF" package="A 3216 [SMD, tantalum]"]
  JACK1 = 2.1mm Barrel Jack with Terminal Block
  J1 = Dagu DGServo 9g header (male) [package=THT]
  D1 = Rectifier Diode [part_number=1N4001 package="Melf DO-213 AB [SMD]"]
  D2 = Rectifier Diode [part_number=1N4001 package="Melf DO-213 AB [SMD]"]

nets:
  N1: U2.Ground, Q1.source, C1.-, C2.-, JACK1.NEG
  N2: U2.Trigger, U2.Threshold, U3.S, C1.+
  N3: U2.Output, R1.Pin_0
  N4: U2.Discharge, R2.Pin_1, D1.cathode, D2.anode
  N5: U2.Vcc_Supply_Voltage, R2.Pin_0, JACK1.POS, J1.pulse
  N6: R1.Pin_1, Q1.gate, C2.+
  N7: Q1.drain, J1.Vcc
  N8: U3.E, D1.anode
  N9: U3.A, D2.cathode
