# Fritzing sketch 12VDC_LED_MOSFET_potentiometer_circuit (saved by Fritzing 0.9.3b)
breadboards: 1

parts:
  JACK1 = 2.1mm Barrel Jack with Terminal Block
  Q1 = Basic FET N-Channel [package="TO220 [THT]"]
  R1 = Resistor [tolerance=±5% resistance=1k package="0402 [SMD]"]
  U1 = POT [package=alps_pot]

nets:
  N1: JACK1.NEG, Q1.source, U1.E
  N2: Q1.gate, R1.Pin_1
  N3: R1.Pin_0, U1.S
