# Fritzing sketch 12VDC_LED_TIP120_circuit (saved by Fritzing 0.9.3b)
breadboards: 1

parts:
  MPX1 = MPX2010 pressure sensor [part_number=MPX]  # not connected
  JACK1 = 2.1mm Barrel Jack with Terminal Block
  Q3 = TIP120 Hi-Current Darlington Transistor
  R6 = Resistor [tolerance=±5% resistance=1k package=THT]
  R7 = Resistor [tolerance=±5% resistance=1k package=THT]
  Q4 = TIP120 Hi-Current Darlington Transistor
  Part2 = Arduino MKR1000

nets:
  GND: JACK1.NEG, Q3.EMITTER, Q4.EMITTER, Part2.GND
  N1: Q3.BASE, R7.Pin_1
  N2: R6.Pin_1, Q4.BASE
  3.3V: Part2.VCC

custom parts:
  Arduino MKR1000: MKR1000 is a powerful board that combines the functionality of the Zero and the Wi-Fi Shield. It is the ideal solution for makers wanting to design IoT projects with minimal previous experience in networking
