# Fritzing sketch MKR_MOSFET (saved by Fritzing 0.9.3b)
breadboards: 1

parts:
  Part2 = Arduino MKR1000
  Accelerometer1 = SparkFun_LIS3DH-Breakout [part_number=SEN-13963]  # not connected

nets:
  N1: Part2.VCC, Part2.D13_RX, Part2.A4/SDA

custom parts:
  Arduino MKR1000: MKR1000 is a powerful board that combines the functionality of the Zero and the Wi-Fi Shield. It is the ideal solution for makers wanting to design IoT projects with minimal previous experience in networking
  SparkFun_LIS3DH-Breakout: The LIS3DH Breakout is a smart, low-power, three-axis, capacitive micro-machined accelerometer with 12 bits of resolution that you can use to add translation detection to your project. It would be classified as a 3DoF, or 3 Degrees of Freedom. Inertial Measurement Units (or IMUs) can provide additional space location data, such as gyroscopic or magnetometric. The LIS3DH provided on this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
