# Fritzing sketch attiny85_mosfet (saved by Fritzing 0.9.9b)
breadboards: 1

parts:
  U1 = attiny85 [package=dip]
  U2 = Voltage Regulator - 5V [package="TO220 [THT]"]
  Q1 = Basic FET N-Channel [package="DPak [SMD]"]
  R1 = Resistor [tolerance=±5% resistance=1k package="0603 [SMD]"]
  R2 = Resistor [tolerance=±5% resistance=10k package="0603 [SMD]"]
  JACK1 = 2.1mm Barrel Jack with Terminal Block

nets:
  N1: U1.Pin_1, R2.Pin_1
  N2: U1.Pin_5, R1.Pin_0
  N3: U1.Pin_8, U2.output_voltage, R2.Pin_0
  N4: U2.input_voltage, JACK1.POS
  GND: U2.GND, Q1.source, JACK1.NEG
  N5: Q1.Gate, R1.Pin_1
