# Fritzing sketch 12VDC_LED_MOSFET_circuit (saved by Fritzing 0.9.3b)
breadboards: 1

parts:
  MPX1 = MPX2010 pressure sensor [part_number=MPX]  # not connected
  JACK1 = 2.1mm Barrel Jack with Terminal Block
  Q1 = Basic FET N-Channel [package="TO220 [THT]"]
  Q2 = Basic FET N-Channel [package="TO220 [THT]"]
  Part2 = Arduino MKR1000

nets:
  GND: JACK1.NEG, Q1.source, Q2.source, Part2.GND
  3.3V: Part2.VCC

custom parts:
  Arduino MKR1000: MKR1000 is a powerful board that combines the functionality of the Zero and the Wi-Fi Shield. It is the ideal solution for makers wanting to design IoT projects with minimal previous experience in networking
