# Fritzing sketch 12VDC_LED_MOSFET_switch_circuit (saved by Fritzing 0.9.3b)
breadboards: 1

parts:
  JACK1 = 2.1mm Barrel Jack with Terminal Block
  Q1 = Basic FET N-Channel [package="TO220 [THT]"]
  R1 = Resistor [tolerance=±5% resistance=1k package="0402 [SMD]"]
  U1 = SWITCH_SPDT [package=kps-1290]
  R2 = Resistor [tolerance=±5% resistance=1k package="0402 [SMD]"]
  R3 = Resistor [tolerance=±5% resistance=1k package="0402 [SMD]"]

nets:
  N1: JACK1.NEG, Q1.source, R3.Pin_1
  N2: Q1.gate, R1.Pin_1
  N3: R1.Pin_0, U1.P
  N4: U1.O, R3.Pin_0
  N5: U1.S, R2.Pin_0
