# Fritzing sketch 555_mosfet_bb (saved by Fritzing 0.9.9b)
breadboards: 1

parts:
  C1 = Tantalum Capacitor [capacitance=100nF voltage=35V package="100 mil [THT, tantalum]"]  # not connected
  U1 = 555 Timer [package="DIP8 [THT]"]
  D1 = Rectifier Diode [part_number=1N4001 package="300 mil [THT]"]
  D2 = Rectifier Diode [part_number=1N4001 package="300 mil [THT]"]
  Q1 = Basic FET N-Channel [package="DPak [SMD]"]  # not connected
  C3 = Tantalum Capacitor [capacitance=10nF voltage=35V package="100 mil [THT, tantalum]"]  # not connected
  R1 = Resistor [tolerance=±5% resistance=1k package="0603 [SMD]"]
  R2 = Resistor [tolerance=±5% resistance=1k package="0603 [SMD]"]
  U2 = POT [package=alps_pot]

nets:
  N1: U1.Output, R1.Pin_0
  N2: U1.Discharge, D1.cathode, D2.anode, R2.Pin_0
  N3: D1.anode, U2.E
  N4: D2.cathode, U2.A
