# Fritzing sketch AS7341_fritzing (saved by Fritzing 0.9.8b)
breadboards: 1

parts:
  Part1 = Adafruit AS7341
  Part2 = Arduino Nano 33 IoT

nets:
  GND: Part1.GND, Part2.GND
  N1: Part1.SDA, Part2.A4/SDA
  VCC: Part1.VCC, Part2.3V3
  N2: Part1.SCL, Part2.A5/SCL

custom parts:
  Arduino Nano 33 IoT: The Arduino Nano 33 IoT is a small, complete, and breadboard-friendly board based on the Arm® Cortex®-M0 32-bit SAMD21. It has onboard WiFi and Bluetooth® connectivity through a u-blox NINA-W10 chipset. Secure communication is ensured through the Microchip® ECC608 crypto chip. It also has 6-axis LSM6DS3 IMU.
